# Fritzing sketch IrrigationCircuit (saved by Fritzing 1.0.2b)
breadboards: 1

parts:
  esp1 = ESP32 DevKitc V4
  S1 = Pushbutton [package=THT]
  RL1 = Solid State High Level Relay Module [package=relay]
  RL2 = Solid State High Level Relay Module [package=relay]
  RL4 = Solid State High Level Relay Module [package=relay]
  RL3 = Solid State High Level Relay Module [package=relay]
  RL5 = Solid State High Level Relay Module [package=relay]
  RL6 = Solid State High Level Relay Module [package=relay]
  RL8 = Solid State High Level Relay Module [package=relay]
  RL7 = Solid State High Level Relay Module [package=relay]
  M1 = ESP-Prog [package=THT]
  S2 = Pushbutton [package=THT]
  S3 = Pushbutton [package=THT]
  S4 = Pushbutton [package=THT]
  S7 = Pushbutton [package=THT]
  S5 = Pushbutton [package=THT]
  S6 = Pushbutton [package=THT]
  S8 = Pushbutton [package=THT]
  RL9 = Solid State High Level Relay Module [package=relay]

nets:
  N1: esp1.IO15, M1.JAG-ESP-TDO-.1
  N2: esp1.IO2, RL8.CH1
  N3: esp1.IO0, RL7.CH1
  N4: esp1.IO4, RL6.CH1
  N5: esp1.IO16, RL5.CH1
  N6: esp1.IO17, RL4.CH1
  N7: esp1.IO5, RL3.CH1
  N8: esp1.IO18, RL2.CH1
  N9: esp1.IO19, RL1.CH1
  N10: esp1.GND, RL1.DC-
  N11: esp1.IO23, RL9.CH1
  N12: esp1.3V3, S1.leg1, S2.leg1, S3.leg1, S4.leg1, S7.leg1, S5.leg1, S6.leg1, S8.leg1
  N13: esp1.VP, S8.leg0
  N14: esp1.VN, S7.leg0
  N15: esp1.IO34, S6.leg0
  N16: esp1.IO35, S5.leg0
  N17: esp1.IO32, S4.leg0
  N18: esp1.IO33, S3.leg0
  N19: esp1.IO25, S2.leg0
  N20: esp1.IO26, S1.leg0
  N21: esp1.IO14, M1.JTAG-ESP_TMS-.1
  N22: esp1.IO12, M1.JTAG-ESP_TDI-.1
  N23: esp1.IO13, M1.JTAG-ESP-TCK-.1
  N24: esp1.5V, RL1.DC+

custom parts:
  ESP32 DevKitc V4: ESP32-DevKitC board with ESP32-WROOM-32 module. ESP32-DevKitC V4 is a small-sized ESP32-based development board produced by Espressif. Most of the pins on the ESP module are broken out to the pin headers on the board. The pins D0, D1, D2, D3, CMD and CLK are used internally for communication between ESP32 and SPI flash memory. They are grouped on both sides near the USB connector. Avoid using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
  Solid State High Level Relay Module: 5V Omron solid state relay 240V 2A output with resistance fuse.
  ESP-Prog: Espressif ESP-Prog board. ESP-Prog is one of Espressif’s development and debugging tools, with functions including automatic firmware downloading, serial communication, and JTAG online debugging. ESP-Prog's automatic firmware downloading and serial communication functions are supported on both the ESP8266 and ESP32 platforms, while the JTAG online debugging is supported only on the ESP32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
